# Fritzing sketch sensoric_schematic (saved by Fritzing 0.9.3b)
breadboards: 1

parts:
  Bauteil1 = InvenSense MPU6050
  Bauteil2 = InvenSense MPU6050
  Bauteil3 = Arduino Uno (Rev3)
  Bauteil4 = Bluetooth Module Breakout - Roving Networks (RN-41)
  R1 = Rotary Potentiometer (Small) [maximum_resistance=100kΩ package=THT]

nets:
  VCC: Bauteil1.VCC, Bauteil2.VCC, Bauteil2.AD0, Bauteil3.5V, Bauteil4.VCC, R1.leg1, R1.leg2
  GND: Bauteil1.GND, Bauteil1.AD0, Bauteil2.GND, Bauteil3.GND, Bauteil4.GND
  N1: Bauteil1.SCL, Bauteil2.SCL, Bauteil3.A5/SCL
  N2: Bauteil1.SDA, Bauteil2.SDA, Bauteil3.A4/SDA
  N3: Bauteil3.A0, R1.wiper
  N4: Bauteil3.D0/RX, Bauteil4.UARTTX
  N5: Bauteil3.D1/TX, Bauteil4.UARTRX
